# Fritzing sketch board (saved by Fritzing 0.9.3b)
breadboards: 1

parts:
  Composant1 = Arduino Uno (Rev3)
  microSD1 = MicroSD Breakout
  LCD1 = LCD screen
  R2 = Resistor [tolerance=±5% resistance=220 package="2010 [SMD]"]
  R3 = Resistor [tolerance=±5% resistance=10k package="2010 [SMD]"]
  S1 = Momentary Switch [package=ksa_sealed_tac_switch]
  S2 = Momentary Switch [package=ksa_sealed_tac_switch]
  R4 = Resistor [tolerance=±5% resistance=10k package="2010 [SMD]"]
  R5 = TRIMPOT [package=trim_pot_pth]

nets:
  N1: Composant1.D8, LCD1.RS
  N2: Composant1.D9_PWM, R3.Pin_1, S1.3
  N3: Composant1.D10_PWM/SS, microSD1.CS
  N4: Composant1.D11_PWM/MOSI, microSD1.DI
  N5: Composant1.D12/MISO, microSD1.DO
  N6: Composant1.D13/SCK, microSD1.CLK
  N7: Composant1.D2, LCD1.DB7
  N8: Composant1.D3_PWM, LCD1.DB6
  N9: Composant1.D4, LCD1.DB5
  N10: Composant1.D5_PWM, LCD1.DB4
  N11: Composant1.D6_PWM, S2.3, R4.Pin_1
  N12: Composant1.D7, LCD1.E
  5V: Composant1.5V, microSD1.5V, LCD1.VDD, R2.Pin_0, S1.1, S2.1, R5.CCW
  GND: Composant1.GND, microSD1.GND, LCD1.VSS, LCD1.R/W, LCD1.LED-, R3.Pin_0, R4.Pin_0, R5.CW
  N13: LCD1.LED+, R2.Pin_1

custom parts:
  MicroSD Breakout: 5V-ready microSD Breakout with Level Shifter

// code stored in the sketch: lcd_and_sd.ino
#include "SdFat.h"
#include <LiquidCrystal.h>

LiquidCrystal lcd(8, 7, 5, 4, 3, 2);
int nextButtonState = 0;

SdFat SD;
int SD_CS_PIN = 10;

int BTN_NEXT_PIN = 6;
int BTN_PLAY_PIN = 9;

File root;
File currentFile;

void setup() {
  // Only for debug
  Serial.begin(9600);

  // SD init
  initializeSD();

  // buttons init
  pinMode(BTN_NEXT_PIN, INPUT);
  pinMode(BTN_PLAY_PIN, INPUT);

  // lcd init
  lcd.begin(16, 2);

  // show first file on lcd
  root = SD.open("/");
  currentFile = getNextFile();
  printFileOnLCD(currentFile);
  
  
}

void loop() {
  int currentButtonState = digitalRead(BUTTON_PIN);
  
  if (currentButtonState != nextButtonState) {
    if (currentButtonState == HIGH) {
      currentFile = getNextFile();
      printFileOnLCD(currentFile);
    }
    nextButtonState = currentButtonState;
  }
}

void initializeSD()
{
  Serial.println("Initializing SD card...");
  pinMode(SD_CS_PIN, OUTPUT);

  if (SD.begin())
  {
    Serial.println("SD card is ready to use.");
  } else
  {
    Serial.println("SD card initialization failed");
    return;
  }
}

File getNextFile() {
  File entry = root.openNextFile();
  if (!entry) {
    root.rewind();
    entry = root.openNextFile();
  } 
  while (entry.isDir()) {
    entry = root.openNextFile();
  } // TODO: what if there's no file? how to stop?
  return entry;
}

void printFileOnLCD(File f) {
  char fileName[16];
  f.getName(fileName, 16);
  lcd.clear();
  lcd.print(fileName);
  lcd.setCursor(0,1);
  lcd.print(f.size());
}
